# Fritzing sketch iohannes (saved by Fritzing 0.7.4b)

parts:
  HC-SR04 = HC-SR04 Ultrasonic Rangefinder
  SparkFun_IOIO = IOIO for Android
  RKI-1004 = Generic Motor Driver
  9V_1800mAH = Power plug
  M1 = DC Motor
  M2 = DC Motor

nets:
  N1: HC-SR04.no_name_yet#8, SparkFun_IOIO.5V, RKI-1004.no_name_yet#connector148-4
  N2: HC-SR04.no_name_yet#9, SparkFun_IOIO.PIN2
  N3: HC-SR04.no_name_yet#10, SparkFun_IOIO.PIN7
  GND: HC-SR04.no_name_yet#11, SparkFun_IOIO.GND, RKI-1004.no_name_yet#connector151-2, 9V_1800mAH.GND
  N4: SparkFun_IOIO.PIN3, RKI-1004.M1A
  N5: SparkFun_IOIO.PIN4, RKI-1004.M1B
  N6: SparkFun_IOIO.PIN5, RKI-1004.M2A
  N7: SparkFun_IOIO.PIN6, RKI-1004.M2B
  VCC: SparkFun_IOIO.VCC, 9V_1800mAH.VCC
  N8: RKI-1004.M1_IN_NEG, M1.pin_2
  N9: RKI-1004.no_name_yet#connector147-9, M1.pin_1
  N10: RKI-1004.no_name_yet#connector148-3, M2.pin_1
  N11: RKI-1004.no_name_yet#connector149-8, M2.pin_2
